// Digital circuit 6502.dig as structural Verilog
// MOS6502
// VHDL code for 6502 from:
// https://github.com/Steve-Teal/mx65
module _6502 (
  input  \Φ0 ,
  input  nRESET,
  input  nNMI,
  input  nIRQ,
  input  RDY,
  output AB0,
  output AB1,
  output AB2,
  output AB3,
  output AB4,
  output AB5,
  output AB6,
  output AB7,
  output AB8,
  output AB9,
  output AB10,
  output AB11,
  output AB12,
  output AB13,
  output AB14,
  output AB15,
  output \Φ2 ,
  output \Φ1 ,
  output R_W,
  output SYNC,
  output DA0,
  output DA1,
  output DA2,
  output DA3,
  output DA4,
  output DA5,
  output DA6,
  output DA7
);

  wire mos6502_1_p8, nr_w;
  wire [7:0] d_out;

  // MOS6502 mos6502_1: pin names not known; wires that end beside it: RDY, nRESET, nNMI, nIRQ, \Φ0 , d_out, {AB15, AB14, AB13, AB12, AB11, AB10, AB9, AB8, AB7, AB6, AB5, AB4, AB3, AB2, AB1, AB0}, mos6502_1_p8, SYNC, \Φ1 , \Φ2 
  Delay delay_1 (.in(mos6502_1_p8), .out(R_W));
  not not_1 (nr_w, mos6502_1_p8);
  BusSplitter #(.Bits(8)) bussplitter_1 (
    .D(d_out), .OE(nr_w), .D0(DA0), .D1(DA1), .D2(DA2), .D3(DA3), .D4(DA4), .D5(DA5), .D6(DA6), .D7(DA7));

  // Other names for the same wires on the sheet: a_out[15:0] = {AB15, AB14, AB13, AB12, AB11, AB10, AB9, AB8, AB7, AB6, AB5, AB4, AB3, AB2, AB1, AB0}

  // Notes on the sheet:
  //   Φ0: Hz: 2
  //   nNMI: default 1
  //   nIRQ: default 1
  //   RDY: default 1
endmodule
