// Digital circuit 6550-layout-1.dig as structural Verilog
// 1kx4 Static RAM (Initialized to Random Values)
module _6550_layout_1 (
  input  R_nW,
  input  A0,
  input  A1,
  input  A2,
  input  A3,
  input  A4,
  input  A5,
  input  A6,
  input  A7,
  input  A8,
  input  A9,
  input  CS1,
  input  CS2,
  input  nCS3,
  input  nCS4,
  input  \Φ2 ,
  output D0,
  output D1,
  output D2,
  output D3
);

  wire and_1_out, nor_1_out;
  wire [3:0] ramsingleportsel_1_d;
  wire [9:0] d_ff_1_q;

  D_FF #(.Bits(10)) d_ff_1 (.D({A9, A8, A7, A6, A5, A4, A3, A2, A1, A0}), .C(\Φ2 ), .Q(d_ff_1_q));  // open: nQ
  and and_1 (and_1_out, CS1, CS2, nor_1_out, \Φ2 );
  nor nor_1 (nor_1_out, nCS3, nCS4);
  RAMSinglePortSel #(.AddrBits(10), .Bits(4)) ramsingleportsel_1 (
    .A(d_ff_1_q), .CS(and_1_out), .WE(~R_nW), .OE(R_nW), .D(ramsingleportsel_1_d));
  BusSplitter #(.Bits(4)) bussplitter_1 (.D(ramsingleportsel_1_d), .OE(R_nW), .D0(D0), .D1(D1), .D2(D2), .D3(D3));
endmodule
