// Digital circuit 6550-layout-3.dig as structural Verilog
// 1kx4 Static RAM (Initialized to Random Values)
module _6550_layout_3 (
  input  R_nW,
  input  CS1,
  input  CS2,
  input  nCS3,
  input  nCS4,
  input  \Φ2 ,
  input  [9:0] A0_A9,
  output D0,
  output D1,
  output D2,
  output D3
);

  wire and_1_out, nor_1_out;
  wire [3:0] bussplitter_1_d;
  wire [9:0] d_ff_1_q;

  BusSplitter #(.Bits(4)) bussplitter_1 (.D(bussplitter_1_d), .OE(R_nW), .D0(D0), .D1(D1), .D2(D2), .D3(D3));
  RAMSinglePortSel #(.AddrBits(10), .Bits(4)) ramsingleportsel_1 (
    .A(d_ff_1_q), .CS(and_1_out), .WE(~R_nW), .OE(R_nW), .D(bussplitter_1_d));
  D_FF #(.Bits(10)) d_ff_1 (.D(A0_A9), .C(\Φ2 ), .Q(d_ff_1_q));  // open: nQ
  and and_1 (and_1_out, \Φ2 , nor_1_out, CS2, CS1);
  nor nor_1 (nor_1_out, nCS4, nCS3);
endmodule
