// Digital circuit DIAG-Keyboard-Dongle.dig as structural Verilog
module DIAG_Keyboard_Dongle (
  input  _2,
  input  _3,
  input  _4,
  input  _5,
  input  _6,
  input  _7,
  input  _8,
  input  _9,
  input  _10,
  input  _1,
  input  CLK,
  output A,
  output B,
  output C,
  output D,
  output E,
  output F,
  output H,
  output J
);

  or or_1 (A, _1, _9);
  or or_2 (B, _2, _10);

  assign C = _3;
  assign D = _4;
  assign E = _5;
  assign F = _6;
  assign H = _7;
  assign J = _8;

  // Notes on the sheet:
  //   The real dongle does not have 
  //   these OR-Gates.
  //   Source:
  //   https://www.c64-wiki.com/wiki/PET_2001#Diagnostic_plugs
endmodule
